// Logisim project CPU.circ as structural Verilog
// 1 Bit Memory Cell
module Mem_1b (
  input  S,
  input  E,
  output Q
);

  wire nand_1_out, nand_2_out, nand_4_out;

  nand nand_1 (nand_1_out, S, E);
  nand nand_2 (nand_2_out, nand_1_out, E);
  nand nand_3 (Q, nand_1_out, nand_4_out);
  nand nand_4 (nand_4_out, Q, nand_2_out);
endmodule

// Memory 1 BYTE
module Mem_1B (
  input  E,
  input  [7:0] I,
  output [7:0] O
);

  Mem_1b mem_1b_1 (.S(I[0]), .E(E), .Q(O[0]));
  Mem_1b mem_1b_2 (.S(I[1]), .E(E), .Q(O[1]));
  Mem_1b mem_1b_3 (.S(I[2]), .E(E), .Q(O[2]));
  Mem_1b mem_1b_4 (.S(I[3]), .E(E), .Q(O[3]));
  Mem_1b mem_1b_5 (.S(I[4]), .E(E), .Q(O[4]));
  Mem_1b mem_1b_6 (.S(I[5]), .E(E), .Q(O[5]));
  Mem_1b mem_1b_7 (.S(I[6]), .E(E), .Q(O[6]));
  Mem_1b mem_1b_8 (.S(I[7]), .E(E), .Q(O[7]));
endmodule
